// Logisim project MCM.circ as structural Verilog: 6 circuits, main circuit main
module main (
);

  _32b_Register u_32b_register_1 ();  // open: D, Q, WEn, Clk
  _32b_Comp__Unsigned u_32b_comp_unsigned_1 ();  // open: A, B, GT, EQ, LT
  _32b_Comp__Signed u_32b_comp_signed_1 ();  // open: A, B, GT, EQ, LT
  _32b_Adder u_32b_adder_1 ();  // open: A, B, A_B
  _32b_Subtractor u_32b_subtractor_1 ();  // open: A, B, A_B
endmodule

module _32b_Register (
  input  [31:0] D,
  input  WEn,
  input  Clk,
  output [31:0] Q
);

  Register #(.width(32)) register_1 (.D(D), .en(WEn), .Q(Q), .clk(Clk));  // open: clr
endmodule

module _32b_Comp__Unsigned (
  input  [31:0] A,
  input  [31:0] B,
  output GT,
  output EQ,
  output LT
);

  Comparator #(.width(32), .mode("unsigned")) comparator_1 (.a(A), .b(B), .gt(GT), .eq(EQ), .lt(LT));
endmodule

module _32b_Comp__Signed (
  input  [31:0] A,
  input  [31:0] B,
  output GT,
  output EQ,
  output LT
);

  Comparator #(.width(32)) comparator_1 (.a(A), .b(B), .gt(GT), .eq(EQ), .lt(LT));
endmodule

module _32b_Adder (
  input  [31:0] A,
  input  [31:0] B,
  output [31:0] A_B
);

  Adder #(.width(32)) adder_1 (.a(A), .b(B), .out(A_B));  // open: cin, cout
endmodule

module _32b_Subtractor (
  input  [31:0] A,
  input  [31:0] B,
  output [31:0] A_B
);

  Subtractor #(.width(32)) subtractor_1 (.a(A), .b(B), .out(A_B));  // open: bin, bout
endmodule
